# Fritzing sketch RetroGnome (saved by Fritzing 0.9.3b)
circuit board: 4.6cm x 8cm
breadboards: 1

parts:
  4x7Seg = TM1637
  S1 = SWITCH-MOMENTARY-2 [package=tactile-pth-12mm]
  Time = Rotary Potentiometer (Small) [maximum_resistance=100kΩ package=THT]
  Tempo = Rotary Potentiometer (Small) [maximum_resistance=100kΩ package=THT]
  Arduino_Nano = Arduino Nano (Rev3.0) (ICSP)
  C1 = Electrolytic Capacitor [capacitance=1µF package="100 mil [THT, electrolytic]"]
  R1 = Resistor [tolerance=±5% resistance=220 package=THT]
  R2 = Resistor [tolerance=±5% resistance=220 package=THT]
  DC_9v = Screw terminal - 2 pins [package=THT]
  Output = screw terminal, 3 pins
  J1 = Piezo Speaker

nets:
  GND: 4x7Seg.GND, S1.1, Time.leg2, Tempo.leg2, Arduino_Nano.GND, R2.Pin_1, DC_9v.pin2, Output.pin2, J1.pin2
  VCC: 4x7Seg.VCC, Time.leg1, Tempo.leg1, Arduino_Nano.5V
  N1: 4x7Seg.DIO, Arduino_Nano.A5
  N2: 4x7Seg.CLK, Arduino_Nano.A4
  N3: S1.2, Arduino_Nano.D2
  N4: Time.wiper, Arduino_Nano.A2
  N5: Tempo.wiper, Arduino_Nano.A7
  N6: Arduino_Nano.D4, R1.Pin_0
  N7: Arduino_Nano.VIN, DC_9v.pin1
  N8: C1.-, Output.pin1
  N9: C1.+, R1.Pin_1, R2.Pin_0
  N10: Output.pin3, J1.pin1

notes:
  RetroGnome v1.0

custom parts:
  TM1637: A 4 7-seg display
